// Logisim project 1 bit ALU.circ as structural Verilog: 1 circuit, main circuit main
module main (
  input  Ci,
  input  F1_1,
  input  F1_4,
  input  Bi,
  input  F2_1,
  input  AC_i,
  input  F2_2,
  input  DR_i,
  input  F2_3,
  input  F3_1,
  input  F3_2,
  input  ac_i_1,
  input  F3_3,
  input  ac_i_1_2,
  input  F3_4,
  output c_i_1,
  output B_i_1,
  output AC
);

  wire adder_1_out, and_1_out, and_2_out, and_3_out, and_4_out, and_5_out, and_6_out, and_7_out, and_8_out,
       and_9_out, not_1_out, or_1_out, subtractor_1_out, xor_1_out;

  Adder #(.width(1)) adder_1 (.a(DR_i), .b(AC_i), .out(adder_1_out), .cin(Ci), .cout(c_i_1));
  Subtractor #(.width(1)) subtractor_1 (.a(DR_i), .b(AC_i), .out(subtractor_1_out), .bin(Bi), .bout(B_i_1));
  or or_1 (or_1_out, DR_i, AC_i);
  xor xor_1 (xor_1_out, DR_i, AC_i);
  not not_1 (not_1_out, AC_i);
  and and_1 (and_1_out, adder_1_out, F1_1);
  and and_2 (and_2_out, DR_i, F1_4);
  and and_3 (and_3_out, subtractor_1_out, F2_1);
  and and_4 (and_4_out, or_1_out, F2_2);
  and and_5 (and_5_out, DR_i, AC_i, F2_3);
  and and_6 (and_6_out, xor_1_out, F3_1);
  and and_7 (and_7_out, not_1_out, F3_2);
  and and_8 (and_8_out, ac_i_1, F3_3);
  and and_9 (and_9_out, ac_i_1_2, F3_4);
  or or_2 (AC, and_1_out, and_2_out, and_3_out, and_4_out, and_5_out, and_6_out, and_7_out, and_8_out, and_9_out);
endmodule
