// Logisim project 16 bit ALU.circ as structural Verilog: 1 circuit, main circuit main
module main (
  input  Ci,
  input  F1_1,
  input  F1_4,
  input  Bi,
  input  F2_1,
  input  F2_2,
  input  F2_3,
  input  F3_1,
  input  F3_2,
  input  F3_3,
  input  F3_4,
  input  FROM_E,
  output out_13,
  output out_14,
  output out_15,
  output out_16,
  output out_17,
  output out_18,
  output out_19,
  output out_20,
  output out_21,
  output out_22,
  output out_23,
  output out_24,
  output E_IN,
  output out_26,
  output out_27,
  output out_28,
  output out_29
);

  wire and_1_out, and_2_out, main_1_c_i_1, main_2_c_i_1, main_3_c_i_1, main_4_c_i_1, main_5_c_i_1,
       main_6_c_i_1, main_7_c_i_1, main_8_c_i_1, main_9_c_i_1, main_10_c_i_1, main_11_c_i_1, main_12_c_i_1,
       main_13_c_i_1, main_14_c_i_1, main_15_c_i_1, undriven, undriven_2, undriven_3, undriven_4, undriven_5,
       undriven_6, undriven_7, undriven_8, undriven_9, undriven_10, undriven_11, undriven_12, undriven_13,
       undriven_14, undriven_15, undriven_16;

  _1_bit_ALU_main main_1 (
    .Ci(Ci), .F1_1(F1_1), .F1_4(F1_4), .Bi(Bi), .F2_1(F2_1), .F2_2(F2_2), .F2_3(F2_3), .F3_1(F3_1),
    .F3_2(F3_2), .ac_i_1(FROM_E), .F3_3(F3_3), .ac_i_1_2(undriven), .F3_4(F3_4), .c_i_1(main_1_c_i_1),
    .AC_i(undriven_3), .AC(out_13));  // open: B_i_1, DR_i
  _1_bit_ALU_main main_2 (
    .Ci(main_13_c_i_1), .F1_1(F1_1), .F1_4(F1_4), .Bi(Bi), .F2_1(F2_1), .F2_2(F2_2), .F2_3(F2_3),
    .F3_1(F3_1), .F3_2(F3_2), .ac_i_1(undriven_11), .F3_3(F3_3), .ac_i_1_2(undriven_8), .F3_4(F3_4),
    .c_i_1(main_2_c_i_1), .AC_i(undriven_4), .AC(out_17));  // open: B_i_1, DR_i
  _1_bit_ALU_main main_3 (
    .Ci(main_14_c_i_1), .F1_1(F1_1), .F1_4(F1_4), .Bi(Bi), .F2_1(F2_1), .F2_2(F2_2), .F2_3(F2_3),
    .F3_1(F3_1), .F3_2(F3_2), .ac_i_1(undriven_16), .F3_3(F3_3), .ac_i_1_2(undriven_2), .F3_4(F3_4),
    .c_i_1(main_3_c_i_1), .AC_i(undriven_14), .AC(out_21));  // open: B_i_1, DR_i
  _1_bit_ALU_main main_4 (
    .Ci(main_15_c_i_1), .F1_1(F1_1), .F1_4(F1_4), .Bi(Bi), .F2_1(F2_1), .F2_2(F2_2), .F2_3(F2_3),
    .F3_1(F3_1), .F3_2(F3_2), .ac_i_1(undriven_10), .F3_3(F3_3), .ac_i_1_2(undriven_9), .F3_4(F3_4),
    .c_i_1(main_4_c_i_1), .AC_i(undriven_15), .AC(out_26));  // open: B_i_1, DR_i
  and and_1 (and_1_out, undriven_3, F3_4);
  _1_bit_ALU_main main_5 (
    .Ci(main_1_c_i_1), .F1_1(F1_1), .F1_4(F1_4), .Bi(Bi), .F2_1(F2_1), .F2_2(F2_2), .F2_3(F2_3), .F3_1(F3_1),
    .F3_2(F3_2), .ac_i_1(undriven_3), .F3_3(F3_3), .ac_i_1_2(undriven_6), .F3_4(F3_4), .c_i_1(main_5_c_i_1),
    .AC_i(undriven), .AC(out_14));  // open: B_i_1, DR_i
  _1_bit_ALU_main main_6 (
    .Ci(main_2_c_i_1), .F1_1(F1_1), .F1_4(F1_4), .Bi(Bi), .F2_1(F2_1), .F2_2(F2_2), .F2_3(F2_3), .F3_1(F3_1),
    .F3_2(F3_2), .ac_i_1(undriven_4), .F3_3(F3_3), .ac_i_1_2(undriven_13), .F3_4(F3_4), .c_i_1(main_6_c_i_1),
    .AC_i(undriven_8), .AC(out_18));  // open: B_i_1, DR_i
  _1_bit_ALU_main main_7 (
    .Ci(main_3_c_i_1), .F1_1(F1_1), .F1_4(F1_4), .Bi(Bi), .F2_1(F2_1), .F2_2(F2_2), .F2_3(F2_3), .F3_1(F3_1),
    .F3_2(F3_2), .ac_i_1(undriven_14), .F3_3(F3_3), .ac_i_1_2(undriven_5), .F3_4(F3_4), .c_i_1(main_7_c_i_1),
    .AC_i(undriven_2), .AC(out_22));  // open: B_i_1, DR_i
  _1_bit_ALU_main main_8 (
    .Ci(main_4_c_i_1), .F1_1(F1_1), .F1_4(F1_4), .Bi(Bi), .F2_1(F2_1), .F2_2(F2_2), .F2_3(F2_3), .F3_1(F3_1),
    .F3_2(F3_2), .ac_i_1(undriven_15), .F3_3(F3_3), .ac_i_1_2(undriven_7), .F3_4(F3_4), .c_i_1(main_8_c_i_1),
    .AC_i(undriven_9), .AC(out_27));  // open: B_i_1, DR_i
  _1_bit_ALU_main main_9 (
    .Ci(main_5_c_i_1), .F1_1(F1_1), .F1_4(F1_4), .Bi(Bi), .F2_1(F2_1), .F2_2(F2_2), .F2_3(F2_3), .F3_1(F3_1),
    .F3_2(F3_2), .ac_i_1(undriven), .F3_3(F3_3), .ac_i_1_2(undriven_11), .F3_4(F3_4), .c_i_1(main_9_c_i_1),
    .AC_i(undriven_6), .AC(out_15));  // open: B_i_1, DR_i
  _1_bit_ALU_main main_10 (
    .Ci(main_6_c_i_1), .F1_1(F1_1), .F1_4(F1_4), .Bi(Bi), .F2_1(F2_1), .F2_2(F2_2), .F2_3(F2_3), .F3_1(F3_1),
    .F3_2(F3_2), .ac_i_1(undriven_8), .F3_3(F3_3), .ac_i_1_2(undriven_16), .F3_4(F3_4),
    .c_i_1(main_10_c_i_1), .AC_i(undriven_13), .AC(out_19));  // open: B_i_1, DR_i
  _1_bit_ALU_main main_11 (
    .Ci(main_7_c_i_1), .F1_1(F1_1), .F1_4(F1_4), .Bi(Bi), .F2_1(F2_1), .F2_2(F2_2), .F2_3(F2_3), .F3_1(F3_1),
    .F3_2(F3_2), .ac_i_1(undriven_2), .F3_3(F3_3), .ac_i_1_2(undriven_10), .F3_4(F3_4),
    .c_i_1(main_11_c_i_1), .AC_i(undriven_5), .AC(out_23));  // open: B_i_1, DR_i
  _1_bit_ALU_main main_12 (
    .Ci(main_8_c_i_1), .F1_1(F1_1), .F1_4(F1_4), .Bi(Bi), .F2_1(F2_1), .F2_2(F2_2), .F2_3(F2_3), .F3_1(F3_1),
    .F3_2(F3_2), .ac_i_1(undriven_9), .F3_3(F3_3), .ac_i_1_2(undriven_12), .F3_4(F3_4),
    .c_i_1(main_12_c_i_1), .AC_i(undriven_7), .AC(out_28));  // open: B_i_1, DR_i
  _1_bit_ALU_main main_13 (
    .Ci(main_9_c_i_1), .F1_1(F1_1), .F1_4(F1_4), .Bi(Bi), .F2_1(F2_1), .F2_2(F2_2), .F2_3(F2_3), .F3_1(F3_1),
    .F3_2(F3_2), .ac_i_1(undriven_6), .F3_3(F3_3), .ac_i_1_2(undriven_4), .F3_4(F3_4), .c_i_1(main_13_c_i_1),
    .AC_i(undriven_11), .AC(out_16));  // open: B_i_1, DR_i
  _1_bit_ALU_main main_14 (
    .Ci(main_10_c_i_1), .F1_1(F1_1), .F1_4(F1_4), .Bi(Bi), .F2_1(F2_1), .F2_2(F2_2), .F2_3(F2_3),
    .F3_1(F3_1), .F3_2(F3_2), .ac_i_1(undriven_13), .F3_3(F3_3), .ac_i_1_2(undriven_14), .F3_4(F3_4),
    .c_i_1(main_14_c_i_1), .AC_i(undriven_16), .AC(out_20));  // open: B_i_1, DR_i
  _1_bit_ALU_main main_15 (
    .Ci(main_11_c_i_1), .F1_1(F1_1), .F1_4(F1_4), .Bi(Bi), .F2_1(F2_1), .F2_2(F2_2), .F2_3(F2_3),
    .F3_1(F3_1), .F3_2(F3_2), .ac_i_1(undriven_5), .F3_3(F3_3), .ac_i_1_2(undriven_15), .F3_4(F3_4),
    .c_i_1(main_15_c_i_1), .AC_i(undriven_10), .AC(out_24));  // open: B_i_1, DR_i
  _1_bit_ALU_main main_16 (
    .Ci(main_12_c_i_1), .F1_1(F1_1), .F1_4(F1_4), .Bi(Bi), .F2_1(F2_1), .F2_2(F2_2), .F2_3(F2_3),
    .F3_1(F3_1), .F3_2(F3_2), .ac_i_1(undriven_7), .F3_3(F3_3), .ac_i_1_2(FROM_E), .F3_4(F3_4),
    .AC_i(undriven_12), .AC(out_29));  // open: c_i_1, B_i_1, DR_i
  and and_2 (and_2_out, undriven_12, F3_3);
  or or_1 (E_IN, and_1_out, and_2_out);
endmodule
