// Logisim project CU.circ as structural Verilog: 1 circuit, main circuit main
module main (
  input  [6:0] External_Map,
  input  CLK,
  input  I,
  input  S,
  input  Z,
  output [2:0] F1,
  output [2:0] F2,
  output [2:0] F3
);

  wire and_1_out, and_2_out, and_3_out, d_ff_1_q, d_ff_2_q, d_ff_3_q, multiplexer_1_out, not_1_out;
  wire [1:0] or_1_out;
  wire [6:0] CAR_q, main_1_output, multiplexer_2_out, rom_1_data_2, SBR_q;
  wire [10:7] rom_1_data;

  D_Flip_Flop d_ff_1 (.clk(CLK), .D(I), .Q(d_ff_1_q));  // open: Qn, preset, en, reset
  D_Flip_Flop d_ff_2 (.clk(CLK), .D(S), .Q(d_ff_2_q));  // open: Qn, preset, en, reset
  D_Flip_Flop d_ff_3 (.clk(CLK), .D(Z), .Q(d_ff_3_q));  // open: Qn, preset, en, reset
  Multiplexer #(.select(2), .enable("false")) multiplexer_1 (
    .in0(1'b1), .in1(d_ff_1_q), .in2(d_ff_2_q), .in3(d_ff_3_q), .out(multiplexer_1_out),
    .sel(rom_1_data[10:9]));
  and and_1 (and_1_out, rom_1_data[7], or_1_out[1]);
  not not_1 (not_1_out, or_1_out[1]);
  INCREMENTER_main main_1 (.INPUT(CAR_q), .OUTPUT(main_1_output));
  and and_2 (and_2_out, multiplexer_1_out, rom_1_data[7], not_1_out);
  and and_3 (and_3_out, multiplexer_1_out, not_1_out);
  Multiplexer #(.select(2), .width(7), .enable("false")) multiplexer_2 (
    .in0(main_1_output), .in1(rom_1_data_2), .in2(SBR_q), .in3(External_Map), .out(multiplexer_2_out),
    .sel(or_1_out));
  Counter #(.width(7), .max('h7f)) CAR (.D(multiplexer_2_out), .Q(CAR_q), .clk(CLK));  // open: load, count, carry, clr
  or or_1 (or_1_out[0], and_3_out, and_1_out);
  Counter #(.width(7), .max('h7f)) SBR (
    .load(and_2_out), .D(main_1_output), .Q(SBR_q));  // open: count, carry, clk, clr
  ROM #(.addrWidth(7), .dataWidth(20)) rom_1 (
    .addr(CAR_q), .data({F1, F2, F3, rom_1_data[10:9], or_1_out[1], rom_1_data[7], rom_1_data_2}));  // open: sel
endmodule
