// Logisim project INCREMENTER.circ as structural Verilog: 1 circuit, main circuit main
module main (
  input  [6:0] INPUT,
  output [6:0] OUTPUT
);

  wire main_1_s, main_2_s, main_3_s, main_4_s, main_5_s, main_6_s;

  half_Adder_main main_1 (.A(1'b1), .B(INPUT[0]), .C(OUTPUT[0]), .S(main_1_s));
  half_Adder_main main_2 (.A(main_1_s), .B(INPUT[1]), .C(OUTPUT[1]), .S(main_2_s));
  half_Adder_main main_3 (.A(main_2_s), .B(INPUT[2]), .C(OUTPUT[2]), .S(main_3_s));
  half_Adder_main main_4 (.A(main_3_s), .B(INPUT[3]), .C(OUTPUT[3]), .S(main_4_s));
  half_Adder_main main_5 (.A(main_4_s), .B(INPUT[4]), .C(OUTPUT[4]), .S(main_5_s));
  half_Adder_main main_6 (.A(main_5_s), .B(INPUT[5]), .C(OUTPUT[5]), .S(main_6_s));
  half_Adder_main main_7 (.A(main_6_s), .B(INPUT[6]), .C(OUTPUT[6]));  // open: S
endmodule
