// Logisim project Input Logic.circ as structural Verilog: 1 circuit, main circuit main
module main (
  input  I0,
  input  I1,
  input  T,
  output L,
  output S1,
  output S0
);

  wire and_2_out, and_3_out, not_1_out;

  not not_1 (not_1_out, I1);
  and and_1 (L, I0, T, not_1_out);
  and and_2 (and_2_out, not_1_out, T);
  and and_3 (and_3_out, I1, I0);
  or or_1 (S0, and_2_out, and_3_out);

  assign S1 = I1;
endmodule
