// Logisim project MAIN PC.circ as structural Verilog: 1 circuit, main circuit main
module main (
);

  wire ALU_ld_ac, clock_1_out, decoder_1_out1, decoder_1_out2, decoder_1_out3, decoder_1_out4,
       decoder_1_out5, decoder_1_out6, decoder_1_out7, decoder_2_out1, decoder_2_out2, decoder_2_out3,
       decoder_2_out4, decoder_2_out5, decoder_2_out6, decoder_2_out7, decoder_3_out1, decoder_3_out2,
       decoder_3_out3, decoder_3_out4, decoder_3_out5, decoder_3_out6, not_1_out, or_1_out, or_2_out,
       or_5_out, or_6_out;
  wire [1:0] or_3_out;
  wire [2:0] CU_f1, CU_f2, CU_f3;
  wire [5:2] bit_extender_1_out;
  wire [10:0] AR_q, multiplexer_1_out, PC_q, undriven;
  wire [15:0] AC_q, ALU_output, bit_extender_1_out_2, bit_extender_2_out, multiplexer_2_out, ram_1_data;

  Clock clock_1 (.out(clock_1_out));
  CU_main CU (
    .External_Map({1'b0, bit_extender_1_out, 2'b00}), .CLK(clock_1_out), .I(bit_extender_1_out_2[15]),
    .S(AC_q[15]), .Z(not_1_out), .F1(CU_f1), .F2(CU_f2), .F3(CU_f3));
  Decoder #(.select(3), .enable("false")) decoder_1 (
    .out1(decoder_1_out1), .out2(decoder_1_out2), .out3(decoder_1_out3), .out4(decoder_1_out4),
    .out5(decoder_1_out5), .out6(decoder_1_out6), .out7(decoder_1_out7), .sel(CU_f1));  // open: out0
  Decoder #(.select(3), .enable("false")) decoder_2 (
    .out1(decoder_2_out1), .out2(decoder_2_out2), .out3(decoder_2_out3), .out4(decoder_2_out4),
    .out5(decoder_2_out5), .out6(decoder_2_out6), .out7(decoder_2_out7), .sel(CU_f2));  // open: out0
  Decoder #(.select(3), .enable("false")) decoder_3 (
    .out1(decoder_3_out1), .out2(decoder_3_out2), .out3(decoder_3_out3), .out4(decoder_3_out4),
    .out5(decoder_3_out5), .out6(decoder_3_out6), .sel(CU_f3));  // open: out0, out7
  Multiplexer #(.width(11), .enable("false")) multiplexer_1 (
    .in0(PC_q), .in1(undriven), .out(multiplexer_1_out), .sel(decoder_1_out5));
  or or_1 (or_1_out, decoder_1_out5, decoder_1_out6);
  assign {bit_extender_1_out_2[15], bit_extender_1_out, bit_extender_1_out_2[10:0]} = {{5{1'b0}}, undriven};  // Bit_Extender bit_extender_1
  Counter #(.width(11), .max('h7ff)) AR (
    .load(or_1_out), .D(multiplexer_1_out), .Q(AR_q));  // open: count, carry, clk, clr
  Counter #(.width(11), .max('h7ff)) PC (
    .load(decoder_3_out6), .D(AR_q), .count(decoder_3_out5), .Q(PC_q));  // open: carry, clk, clr
  or or_2 (or_2_out, decoder_2_out4, decoder_2_out5, decoder_2_out7);
  assign bit_extender_2_out = {{5{1'b0}}, PC_q};  // Bit_Extender bit_extender_2
  or or_3 (or_3_out[0], decoder_2_out6, decoder_2_out5);
  or or_4 (or_3_out[1], decoder_2_out5, decoder_2_out4);
  Multiplexer #(.select(2), .width(16), .enable("false")) multiplexer_2 (
    .in1(bit_extender_2_out), .in2(ram_1_data), .in3(AC_q), .out(multiplexer_2_out), .sel(or_3_out));  // open: in0
  or or_5 (or_5_out, decoder_1_out7, decoder_2_out4);
  Counter #(.width(16), .max('hffff)) DR (
    .load(or_2_out), .D(multiplexer_2_out), .count(decoder_2_out6),
    .Q({bit_extender_1_out_2[15], bit_extender_1_out, bit_extender_1_out_2[10:0]}));  // open: carry, clk, clr
  RAM #(.addrWidth(11), .dataWidth(16), .bus("separate")) ram_1 (
    .addr(AR_q), .din({bit_extender_1_out_2[15], bit_extender_1_out, bit_extender_1_out_2[10:0]}),
    .data(ram_1_data), .str(decoder_1_out7), .sel(or_5_out), .ld(decoder_2_out4));  // open: clk, clr
  ALU_main ALU (
    .AC(AC_q), .DR({bit_extender_1_out_2[15], bit_extender_1_out, bit_extender_1_out_2[10:0]}),
    .ADD(decoder_1_out1), .SUB(decoder_2_out1), .OR(decoder_2_out2), .AND(decoder_2_out3),
    .XOR(decoder_3_out1), .COM(decoder_3_out2), .SHL(decoder_3_out3), .SHR(decoder_3_out4),
    .in_11(decoder_1_out4), .OUTPUT(ALU_output), .LD_AC(ALU_ld_ac));
  Counter #(.width(16), .max('hffff)) AC (
    .load(ALU_ld_ac), .D(ALU_output), .count(decoder_1_out3), .Q(AC_q), .clr(decoder_1_out2));  // open: carry, clk
  not not_1 (not_1_out, or_6_out);
  or or_6 (or_6_out, AC_q[0], AC_q[1], AC_q[2], AC_q[3], AC_q[4], AC_q[5], AC_q[6], AC_q[7], AC_q[8], AC_q[9], AC_q[10], AC_q[11], AC_q[12], AC_q[13], AC_q[14], AC_q[15]);
endmodule
