// Logisim project half Adder.circ as structural Verilog: 1 circuit, main circuit main
module main (
  input  A,
  input  B,
  output C,
  output S
);

  xor xor_1 (S, B, A);
  and and_1 (C, A, B);
endmodule
